# Fritzing sketch Config_Connection HC-05 (saved by Fritzing 0.8.7b)
breadboards: 1

parts:
  Componente1 = Arduino Uno (Rev3)
  Componente2 = HC-05 [part_number=HC-05 package="breakout board"]

nets:
  N1: Componente1.D2, Componente2.TXD
  N2: Componente1.D3_PWM, Componente2.RXD
  N3: Componente1.3V3, Componente2.Key
  5V: Componente1.5V, Componente2.VCC
  GND: Componente1.GND, Componente2.GND

custom parts:
  HC-05: A commonly available HC-05 Bluetooth breakout board.
