# Fritzing sketch Untitled Sketch 2 (saved by Fritzing 0.8.7b)
breadboards: 1

parts:
  Componente1 = Arduino Uno (Rev3) - ICSP
  KY-1 = Keyes Relay [package=THT]
  Q1 = PNP-Transistor [package="SOT-23 [SMD]"]

nets:
  N1: Componente1.5V, Q1.0
  N2: Componente1.GND, Q1.2
  N3: KY-1.NO, Q1.1

notes:
  12V (FONTE)
  GND (FONTE)
  COLETOR
  EMISOR
  BASE

custom parts:
  Keyes Relay: The Keyes 5V relay module is suitable for SCM development, home appliance control. It uses a 5V~12V TIL control signal which can control DC / AC signal.
